# Fritzing sketch colorchron (saved by Fritzing 0.9.3b)
breadboards: 1

parts:
  MCU1 = Raspberry Pi Zero
  U2 = 74AHCT125 [package=dil14]
  NEOPIXEL1 = Neopixel Strip -- Black (60/m) [part_number=1461]
  Part2 = Adafruit VCNL4010 Proximity and Light sensor [part_number="Adafruit #466"]

nets:
  N1: MCU1.pin_1, Part2.3.3V
  VCC: MCU1.pin_2, U2.VCC, NEOPIXEL1.+5V
  N2: MCU1.pin_3, Part2.SDA
  N3: MCU1.pin_5, Part2.SCL
  GND: MCU1.pin_6, MCU1.pin_9, U2.1A, U2.GND, NEOPIXEL1.GND, Part2.GND
  N4: MCU1.pin_12, U2.1Y
  N5: U2.2A, NEOPIXEL1.DI

custom parts:
  74AHCT125: 74AHCT125 IC BUF NON-INVERT 5.5V 14DIP
  Neopixel Strip -- Black (60/m): Neopixel Strip, Black, 60 pixels per meter.
  Adafruit VCNL4010 Proximity and Light sensor: The VCNL4010 sensor is a nice way to add a small-distance proximity sensor to your microcontroller project. For longer distances (in the range of cm, you can use a SHARP IR distance sensor, but those are only good if the object is over 10 cm away. The VCNL4010 is designed for much shorter distances, no more than 200mm (about 7.5") and under our experimentation we found it worked best at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
