# Fritzing sketch level-shift-board (saved by Fritzing 0.9.3b)
perfboards: 1

parts:
  U1 = 74AHCT125 [package=dil14]
  MCU1 = Raspberry Pi Zero
  NEOPIXEL1 = Neopixel Strip -- Black (60/m) [part_number=1461]
  Part1 = Adafruit VCNL4010 Proximity and Light sensor [part_number="Adafruit #466"]

nets:
  N1: U1.1A, U1.GND, MCU1.pin_2, MCU1.pin_4
  N2: U1.1Y, MCU1.pin_12
  N3: U1.2A, NEOPIXEL1.DI
  VCC: U1.VCC, NEOPIXEL1.+5V
  N4: MCU1.pin_1, Part1.3.3V
  N5: MCU1.pin_3, Part1.SDA
  N6: MCU1.pin_5, Part1.SCL
  N7: MCU1.pin_11, Part1.GND

notes:
  Wires going from pi to PCB board attach at 3 pins. Matched outgoing wires to LED strip come off 3 directly adjacent pins. Straight wires are soldered into PCB.

custom parts:
  74AHCT125: 74AHCT125 IC BUF NON-INVERT 5.5V 14DIP
  Neopixel Strip -- Black (60/m): Neopixel Strip, Black, 60 pixels per meter.
  Adafruit VCNL4010 Proximity and Light sensor: The VCNL4010 sensor is a nice way to add a small-distance proximity sensor to your microcontroller project. For longer distances (in the range of cm, you can use a SHARP IR distance sensor, but those are only good if the object is over 10 cm away. The VCNL4010 is designed for much shorter distances, no more than 200mm (about 7.5") and under our experimentation we found it worked best at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
